# Fritzing sketch Scheme (saved by Fritzing 0.9.3b)
breadboards: 1

parts:
  LED1 = LED - 5mm [color="Red (633nm)" package="5 mm [THT]"]
  Rezistor = Resistor [tolerance=±5% resistance=10k package=THT]
  Buzzer = Piezo Speaker
  Servo = Basic Servo
  Button = Pushbutton [package="[THT]"]
  Power_convertor = HLK-PM01
  Servo_2 = Basic Servo
  Arduino_Leonardo = Arduino Leonardo (Rev3b)

nets:
  GND: LED1.cathode, Rezistor.Pin_1, Buzzer.pin1, Servo.gnd, Power_convertor.-Vo, Servo_2.gnd, Arduino_Leonardo.GND
  N1: LED1.anode, Arduino_Leonardo.D13_PWM
  N2: Rezistor.Pin_0, Button.Pin_1, Button.Pin_2, Arduino_Leonardo.D5_PWM
  N3: Buzzer.pin2, Arduino_Leonardo.D10_PWM/A10
  VCC: Servo.vcc, Power_convertor.+Vo, Servo_2.vcc
  N4: Servo.pulse, Arduino_Leonardo.D3_PWM/SCL, Arduino_Leonardo.SCL
  N5: Button.Pin_3, Button.Pin_4, Arduino_Leonardo.5V
  N6: Servo_2.pulse, Arduino_Leonardo.D9_PWM/A9
